# Fritzing sketch mlb_proto_board (saved by Fritzing 0.9.4)
perfboards: 1

parts:
  MPU9250_MPU-1 = SparkFun IMU Breakout - MPU-9250 [part_number=" SEN-13762"]  # not connected
  Adafruit_HUZZAH_ESP8266_Breakout1 = Adafruit HUZZAH ESP8266 Breakout [part_number=2471]
  Part1 = BME280 Breakout  # not connected
  J1 = male pin header, 18 pins [form="♂ (male)"]  # not connected
  J2 = male pin header, 18 pins [form="♂ (male)"]
  J3 = male pin header, 18 pins [form="♂ (male)"]  # not connected
  J4 = male pin header, 18 pins [form="♂ (male)"]
  J5 = female pin header, 6 pins [form="♀ (female)"]  # not connected
  J6 = female pin header, 5 pins [form="♀ (female)"]
  J7 = female pin header, 4 pins [form="♀ (female)"]
  J9 = male pin header, 2 pins [form="♂ (male)"]  # not connected
  J11 = male pin header, 2 pins [form="♂ (male)"]
  J12 = male pin header, 2 pins [form="♂ (male)"]
  J8 = female pin header, 5 pins [form="♀ (female)"]
  J13 = male pin header, 3 pins [form="♂ (male)"]

nets:
  N1: Adafruit_HUZZAH_ESP8266_Breakout1.GND, J4.pin11
  N2: Adafruit_HUZZAH_ESP8266_Breakout1.TX, J11.pin2
  N3: Adafruit_HUZZAH_ESP8266_Breakout1.RX, J11.pin1
  N4: Adafruit_HUZZAH_ESP8266_Breakout1.V+, J4.pin12
  N5: J2.pin5, J7.pin4, J8.pin3
  N6: J2.pin6, J7.pin3, J8.pin4
  N7: J2.pin8, J6.pin1, J8.pin1
  N8: J2.pin11, J13.pin3
  N9: J2.pin12, J8.pin5
  N10: J4.pin7, J7.pin2
  N11: J4.pin13, J12.pin1
  N12: J4.pin14, J12.pin2
